# Fritzing sketch BoardModel (saved by Fritzing 0.9.3b)
circuit board: 9.33826cm x 6.32568cm

parts:
  HC-06/05 = Bluetooth HC-05 Macho
  Arduino(nano/uno) = Arduino Uno (Rev3) - ICSP
  SERVO = Dagu DGServo 9g header connector (female) [package=THT]
  ESC = Dagu DGServo 9g header connector (female) [package=THT]

nets:
  N1: HC-06/05.TXD, Arduino(nano/uno).D3_PWM
  N2: HC-06/05.RXD, Arduino(nano/uno).D2
  VCC: HC-06/05.VCC, Arduino(nano/uno).5V, SERVO.Vcc, ESC.Vcc
  GND: HC-06/05.GND, Arduino(nano/uno).GND, SERVO.gnd, ESC.gnd
  N3: Arduino(nano/uno).D5_PWM, ESC.pulse
  N4: Arduino(nano/uno).D6_PWM, SERVO.pulse
